# Fritzing sketch totalCircuit (saved by Fritzing 0.8.7b)
breadboards: 2

parts:
  부품1 = Arduino Uno (Rev3) - ICSP
  BT1 = Bluetooth HC-06d [package=THT]
  U1 = prefix0000
  M1 = Stepper Motor - Unipolar
  BAT1 = Battery Holders [package=lipo-1100mAh]
  M2 = DC Motor  # not connected
  부품3 = Solid State High Level Relay Module [package=relay]
  부품4 = Solid State High Level Relay Module [package=relay]
  BAT2 = Battery Holders [package=lipo-1100mAh]
  S1 = Square Pushbutton  # not connected

nets:
  N1: 부품1.ICSP_MISO, 부품1.D12/MISO, BT1.RXD
  N2: 부품1.ICSP_MOSI, 부품1.D11_PWM/MOSI, BT1.TXD
  N3: 부품1.D2, U1.connector9
  N4: 부품1.D3_PWM, U1.connector11
  N5: 부품1.D4, 부품3.CH1
  N6: 부품1.D5_PWM, 부품4.CH1
  5V: 부품1.5V, BT1.VCC, U1.connector7, 부품3.DC+, 부품4.DC+
  GND: 부품1.GND, BT1.GND, 부품3.DC-, 부품4.DC-, BAT2.-
  N7: 부품1.VIN, BAT2.+
  N8: U1.connector0, M1.D
  N9: U1.connector1, M1.B
  N10: U1.connector2, M1.C
  N11: U1.connector3, M1.A
  N12: U1.connector4, BAT1.+
  N13: U1.connector5, BAT1.-
  N14: 부품3.A1, 부품4.A1

custom parts:
  Bluetooth HC-06d: Bluetooth HC-06 - face down, pins down 16.5mm x 37.5mm PCB
  Solid State High Level Relay Module: 5V Omron solid state relay 240V 2A output with resistance fuse.
